# Fritzing sketch Wemos LED Driver (saved by Fritzing 0.9.3b)
breadboards: 1

parts:
  WeMos_D1_Mini2 = WeMos D1 Mini
  Part3 = 16-Channel 12-bit PWM Servo Driver - I2C [part_number=815]
  DS2 = DS18B20 1-Wire Temperature Sensor [part_number=DS18B20]
  Part4 = Breadboard Power Supply Board SMD
  U1 = LDD700-L
  Q1 = Basic FET P-Channel [package="TO220 [THT]"]
  F1 = Fan - Ventilador [package=THT]
  R1 = Resistor [tolerance=±5% resistance=220 package="0402 [SMD]"]

nets:
  3.3V: WeMos_D1_Mini2.3V3, Part3.VCC, DS2.VDD, Part4.VCC
  N1: WeMos_D1_Mini2.D1, Part3.SCL
  N2: WeMos_D1_Mini2.D2, Part3.SDA
  N3: WeMos_D1_Mini2.D4, Q1.gate, R1.Pin_1
  N4: WeMos_D1_Mini2.D7, DS2.DQ
  GND: WeMos_D1_Mini2.G, Part3.GND, Part3.OE, DS2.GND, Part4.GND, U1.-Vin, Q1.source, R1.Pin_0
  N5: Part3.PWM0, U1.DIM
  12V: Part4.VIN, F1.5V
  N6: Q1.drain, F1.GND

custom parts:
  16-Channel 12-bit PWM Servo Driver - I2C: You want to make a cool robot, maybe a hexapod walker, or maybe just a piece of art with a lot of moving parts. Or maybe you want to drive a lot of LEDs with precise PWM output. Using only two pins, control 16 free-running PWM outputs! You can even chain up 62 breakouts to control up to 992 PWM outputs.
  LDD700-L: MeanWell LDD-700L LED Driver
  Fan - Ventilador: Ventilador de 2 pines, se encuentra comunmente en computadoras de escritorio
